// Logisim project MATRIX_MULTIPLICATION.circ as structural Verilog: 1 circuit, main circuit main
module main (
  input  [5:0] _1,
  input  [5:0] _2,
  input  [5:0] _1_2,
  input  [5:0] _1_3,
  input  [5:0] _2_2,
  input  [5:0] in_6,
  input  [5:0] in_7,
  input  [5:0] _2_3,
  input  in_9,
  input  [1:0] in_10,
  input  in_11,
  input  in_12,
  input  in_13,
  input  in_14,
  input  [1:0] in_15,
  input  in_16,
  input  in_17,
  input  in_18,
  input  in_19,
  input  in_20,
  input  in_21,
  output [5:0] RESULTANT_MATRIX,
  output [5:0] out_23,
  output [5:0] out_24,
  output [5:0] out_25,
  output [5:0] in_loop,
  output [5:0] out_27,
  output [5:0] out_28,
  output [5:0] out_29,
  output out_30,
  output [5:0] out_31,
  output [5:0] out_32,
  output [5:0] out_33,
  output [1:0] must_be_11_at_beginning,
  output out_35,
  output [5:0] out_36,
  output [5:0] out_37
);

  wire clock_1_out, counter_1_q, counter_3_q, not_1_out;
  wire [1:0] counter_2_q;
  wire [5:0] register_2_q, register_3_q;

  Counter #(.width(1), .max('h1), .trigger("falling")) counter_1 (
    .D(in_9), .Q(counter_1_q), .clk(clock_1_out));  // open: load, count, carry, clr
  Multiplexer #(.width(6), .enable("false")) multiplexer_1 (.in0(_1), .in1(_2), .out(in_loop), .sel(counter_1_q));
  Multiplexer #(.width(6), .enable("false")) multiplexer_2 (.in0(_2_2), .in1(in_6), .out(out_32), .sel(counter_1_q));
  Clock clock_1 (.out(clock_1_out));
  Counter #(.width(2), .max('h3), .trigger("falling")) counter_2 (
    .D(in_10), .Q(counter_2_q), .clk(clock_1_out));  // open: load, count, carry, clr
  Multiplier #(.width(6)) multiplier_1 (.a(in_loop), .b(out_27), .out(out_31));  // open: cin, cout
  Multiplier #(.width(6)) multiplier_2 (.a(out_27), .b(out_32), .out(out_37));  // open: cin, cout
  Multiplexer #(.select(2), .width(6), .enable("false")) multiplexer_3 (
    .in0(_1_2), .in1(in_7), .in2(_1_3), .in3(_2_3), .out(out_27), .sel(counter_2_q));
  Register #(.width(6), .trigger("falling")) register_1 (
    .D(out_31), .en(counter_3_q), .Q(out_33), .clk(clock_1_out));  // open: clr
  Counter #(.width(1), .max('h1), .trigger("falling")) counter_3 (
    .D(in_17), .Q(counter_3_q), .clk(clock_1_out));  // open: load, count, carry, clr
  Register #(.width(6), .trigger("falling")) register_2 (
    .D(out_37), .en(counter_3_q), .Q(register_2_q), .clk(clock_1_out));  // open: clr
  Register #(.width(6), .trigger("falling")) register_3 (
    .D(out_37), .en(not_1_out), .Q(register_3_q), .clk(clock_1_out));  // open: clr
  not not_1 (not_1_out, counter_3_q);
  Register #(.width(6), .trigger("falling")) register_4 (
    .D(out_31), .en(not_1_out), .Q(out_28), .clk(clock_1_out));  // open: clr
  Adder #(.width(6)) adder_1 (.a(out_28), .b(out_33), .out(out_29));  // open: cin, cout
  Adder #(.width(6)) adder_2 (.a(register_2_q), .b(register_3_q), .out(out_36));  // open: cin, cout
  Register #(.width(6), .trigger("high")) register_5 (
    .D(out_29), .en(out_30), .Q(RESULTANT_MATRIX), .clk(in_16));  // open: clr
  Register #(.width(6), .trigger("high")) to_store_21 (.D(out_36), .en(out_35), .Q(out_24), .clk(in_16));  // open: clr
  Register #(.width(6), .trigger("high")) to_store_22 (.D(out_36), .en(out_30), .Q(out_25), .clk(in_16));  // open: clr
  Register #(.width(6), .trigger("high")) to_store_11 (.D(out_29), .en(out_35), .Q(out_23), .clk(in_16));  // open: clr
  Multiplexer #(.select(2), .enable("false")) multiplexer_4 (
    .in0(in_11), .in1(in_12), .in2(in_13), .in3(in_14), .out(out_30), .sel(must_be_11_at_beginning));
  Counter #(.width(2), .max('h3), .trigger("falling")) counter_4 (
    .D(in_15), .Q(must_be_11_at_beginning), .clk(clock_1_out));  // open: load, count, carry, clr
  Multiplexer #(.select(2), .enable("false")) multiplexer_5 (
    .in0(in_18), .in1(in_19), .in2(in_20), .in3(in_21), .out(out_35), .sel(must_be_11_at_beginning));

  // Notes on the sheet:
  //   1
  //   1
  //   MATRIX A
  //   Counter
  //   First row
  //   second row in loop
  //   all four in loop
  //   counter
  //   MATRIX B
  //   2
  //   To store 12
endmodule
